# Fritzing sketch stm32 (saved by Fritzing 0.9.3b)
breadboards: 1

parts:
  U1 = Carte NUCLEO H755ZI-Q
  부품1 = Bluetooth HC-05 Macho
  M1 = linear actuator [package=THT]
  S1 = H-Bridge with L298N
  VCC1 = Battery block 9V

nets:
  5V: U1.5V, 부품1.VCC, S1.5V
  GND: U1.GND, 부품1.GND, S1.GND, VCC1.-
  N1: M1.pin1, S1.M2-02
  N2: M1.pin2, S1.M2-01
  N3: S1.12V, VCC1.+

custom parts:
  Carte NUCLEO H755ZI-Q: Carte prototype double coeurs ARM
  linear actuator: Generic linear actuator.
  H-Bridge with L298N: h-bridge
